# Fritzing sketch fritzing (saved by Fritzing 0.9.3b)
breadboards: 1

parts:
  MCU1 = Raspberry Pi Zero
  Teensy_3_1 = Teensy 3.1

nets:
  N1: MCU1.pin_2, MCU1.pin_4, Teensy_3_1.Vin
  N2: MCU1.pin_6, Teensy_3_1.GND
  N3: MCU1.pin_8, Teensy_3_1.D0
  N4: MCU1.pin_10, Teensy_3_1.D1
